# Fritzing sketch ebikePCB (saved by Fritzing 0.9.3b)
circuit board: 5.6cm x 5.6cm
breadboards: 1

parts:
  Potentiometer = Rotary Potentiometer (Small) [maximum_resistance=100kΩ package=THT]
  Arduino_Nano = Arduino Nano (Rev3.0) (ICSP)
  ESC = Basic Servo

nets:
  GND: Potentiometer.leg1, Arduino_Nano.GND, ESC.gnd
  N1: Potentiometer.wiper, Arduino_Nano.A0
  5V: Potentiometer.leg2, Arduino_Nano.5V, ESC.vcc
  N2: Arduino_Nano.D9, ESC.pulse

notes:
  EConvrsn by Javier Garcia
